// Logisim project domaci1.circ as structural Verilog: 1 circuit, main circuit main
module main (
  input  x1,
  input  x2,
  input  x3,
  input  x4,
  input  x5,
  output out_6
);

  wire and_1_out, not_1_out, not_2_out;

  not not_1 (not_1_out, x3);
  // Probe on and_1_out
  and and_1 (and_1_out, x1, x2, not_1_out);
  not not_2 (not_2_out, x5);
  or or_1 (out_6, and_1_out, x4, not_2_out);
endmodule
